// Logisim project MUX LUT 7 segmentos.circ as structural Verilog: 3 circuits, main circuit main
module main (
  input  [3:0] in_1,
  input  [3:0] in_2,
  output out_3
);

  wire _0_cout, _1_cout, _2_cout;
  wire [3:0] _0_sum;

  somador _0 (.A(in_1[0]), .B(in_2[0]), .Cin(1'b0), .Sum(_0_sum[0]), .Cout(_0_cout));
  somador _1 (.A(in_1[1]), .B(in_2[1]), .Cin(_0_cout), .Sum(_0_sum[1]), .Cout(_1_cout));
  somador _2 (.A(in_1[2]), .B(in_2[2]), .Cin(_1_cout), .Sum(_0_sum[2]), .Cout(_2_cout));
  somador _3 (.A(in_1[3]), .B(in_2[3]), .Cin(_2_cout), .Sum(_0_sum[3]), .Cout(out_3));
  Hex_Digit_Display hex_digit_display_1 (.value(_0_sum));  // open: dp
endmodule

module somador (
  input  A,
  input  B,
  input  Cin,
  output Sum,
  output Cout
);

  Multiplexer #(.select(3)) multiplexer_1 (
    .in0(1'b0), .in1(1'b1), .in2(1'b1), .in3(1'b0), .in4(1'b1), .in5(1'b0), .in6(1'b0), .in7(1'b1),
    .out(Sum), .sel({A, B, Cin}));  // open: en
  Multiplexer #(.select(3)) multiplexer_2 (
    .in0(1'b0), .in1(1'b0), .in2(1'b0), .in3(1'b1), .in4(1'b0), .in5(1'b1), .in6(1'b1), .in7(1'b1),
    .out(Cout), .sel({A, B, Cin}));  // open: en
endmodule

module _7segment (
  input  [3:0] in_1,
  input  [3:0] in_2,
  output out_3
);

  wire _0_cout, _1_cout, _2_cout, multiplexer_1_out, multiplexer_2_out, multiplexer_3_out, multiplexer_4_out,
       multiplexer_5_out, multiplexer_6_out, multiplexer_7_out;
  wire [3:0] _0_sum;

  Multiplexer #(.select(4)) multiplexer_1 (
    .in0(1'b1), .in1(1'b0), .in2(1'b1), .in3(1'b1), .in4(1'b0), .in5(1'b1), .in6(1'b1), .in7(1'b1),
    .in8(1'b1), .in9(1'b1), .in10(1'b1), .in11(1'b0), .in12(1'b1), .in13(1'b0), .in14(1'b1), .in15(1'b1),
    .out(multiplexer_1_out), .sel(_0_sum));  // open: en
  Multiplexer #(.select(4)) multiplexer_2 (
    .in0(1'b1), .in1(1'b1), .in2(1'b1), .in3(1'b1), .in4(1'b1), .in5(1'b0), .in6(1'b0), .in7(1'b1),
    .in8(1'b1), .in9(1'b1), .in10(1'b1), .in11(1'b0), .in12(1'b0), .in13(1'b1), .in14(1'b0), .in15(1'b0),
    .out(multiplexer_2_out), .sel(_0_sum));  // open: en
  somador _0 (.A(in_1[0]), .B(in_2[0]), .Cin(1'b0), .Sum(_0_sum[0]), .Cout(_0_cout));
  Multiplexer #(.select(4)) multiplexer_3 (
    .in0(1'b1), .in1(1'b1), .in2(1'b0), .in3(1'b1), .in4(1'b1), .in5(1'b1), .in6(1'b1), .in7(1'b1),
    .in8(1'b1), .in9(1'b1), .in10(1'b1), .in11(1'b1), .in12(1'b0), .in13(1'b1), .in14(1'b0), .in15(1'b0),
    .out(multiplexer_3_out), .sel(_0_sum));  // open: en
  somador _1 (.A(in_1[1]), .B(in_2[1]), .Cin(_0_cout), .Sum(_0_sum[1]), .Cout(_1_cout));
  Multiplexer #(.select(4)) multiplexer_4 (
    .in0(1'b1), .in1(1'b0), .in2(1'b1), .in3(1'b1), .in4(1'b0), .in5(1'b1), .in6(1'b1), .in7(1'b0),
    .in8(1'b1), .in9(1'b1), .in10(1'b0), .in11(1'b1), .in12(1'b1), .in13(1'b1), .in14(1'b1), .in15(1'b0),
    .out(multiplexer_4_out), .sel(_0_sum));  // open: en
  somador _2 (.A(in_1[2]), .B(in_2[2]), .Cin(_1_cout), .Sum(_0_sum[2]), .Cout(_2_cout));
  Multiplexer #(.select(4)) multiplexer_5 (
    .in0(1'b1), .in1(1'b0), .in2(1'b1), .in3(1'b0), .in4(1'b0), .in5(1'b0), .in6(1'b1), .in7(1'b0),
    .in8(1'b1), .in9(1'b0), .in10(1'b1), .in11(1'b1), .in12(1'b1), .in13(1'b1), .in14(1'b1), .in15(1'b1),
    .out(multiplexer_5_out), .sel(_0_sum));  // open: en
  somador _3 (.A(in_1[3]), .B(in_2[3]), .Cin(_2_cout), .Sum(_0_sum[3]), .Cout(out_3));
  Multiplexer #(.select(4)) multiplexer_6 (
    .in0(1'b1), .in1(1'b0), .in2(1'b0), .in3(1'b0), .in4(1'b1), .in5(1'b1), .in6(1'b1), .in7(1'b0),
    .in8(1'b1), .in9(1'b1), .in10(1'b1), .in11(1'b1), .in12(1'b1), .in13(1'b0), .in14(1'b1), .in15(1'b1),
    .out(multiplexer_6_out), .sel(_0_sum));  // open: en
  Multiplexer #(.select(4)) multiplexer_7 (
    .in0(1'b0), .in1(1'b0), .in2(1'b1), .in3(1'b1), .in4(1'b1), .in5(1'b1), .in6(1'b1), .in7(1'b0),
    .in8(1'b1), .in9(1'b1), .in10(1'b1), .in11(1'b1), .in12(1'b0), .in13(1'b1), .in14(1'b1), .in15(1'b1),
    .out(multiplexer_7_out), .sel(_0_sum));  // open: en
  _7_Segment_Display u_7_segment_display_1 (
    .g(multiplexer_7_out), .f(multiplexer_6_out), .a(multiplexer_1_out), .b(multiplexer_2_out),
    .e(multiplexer_5_out), .d(multiplexer_4_out), .c(multiplexer_3_out));  // open: dp
endmodule
