// Logisim project MUX LUT.circ as structural Verilog: 8 circuits, main circuit main
module main (
  input  [7:0] in_1,
  input  [7:0] in_2,
  output [7:0] out_3,
  output out_4
);

  wire _0_cout, _1_cout, _2_cout, _3_cout, _4_cout, _5_cout, _6_cout;

  somador _0 (.A(in_1[0]), .B(in_2[0]), .Cin(1'b0), .Sum(out_3[0]), .Cout(_0_cout));
  somador _1 (.A(in_1[1]), .B(in_2[1]), .Cin(_0_cout), .Sum(out_3[1]), .Cout(_1_cout));
  somador _2 (.A(in_1[2]), .B(in_2[2]), .Cin(_1_cout), .Sum(out_3[2]), .Cout(_2_cout));
  somador _3 (.A(in_1[3]), .B(in_2[3]), .Cin(_2_cout), .Sum(out_3[3]), .Cout(_3_cout));
  somador _4 (.A(in_1[4]), .B(in_2[4]), .Cin(_3_cout), .Sum(out_3[4]), .Cout(_4_cout));
  somador _5 (.A(in_1[5]), .B(in_2[5]), .Cin(_4_cout), .Sum(out_3[5]), .Cout(_5_cout));
  somador _6 (.A(in_1[6]), .B(in_2[6]), .Cin(_5_cout), .Sum(out_3[6]), .Cout(_6_cout));
  somador _7 (.A(in_1[7]), .B(in_2[7]), .Cin(_6_cout), .Sum(out_3[7]), .Cout(out_4));
endmodule

module somador (
  input  A,
  input  B,
  input  Cin,
  output Sum,
  output Cout
);

  Multiplexer #(.select(3)) multiplexer_1 (
    .in0(1'b0), .in1(1'b1), .in2(1'b1), .in3(1'b0), .in4(1'b1), .in5(1'b0), .in6(1'b0), .in7(1'b1),
    .out(Sum), .sel({A, B, Cin}));  // open: en
  Multiplexer #(.select(3)) multiplexer_2 (
    .in0(1'b0), .in1(1'b0), .in2(1'b0), .in3(1'b1), .in4(1'b0), .in5(1'b1), .in6(1'b1), .in7(1'b1),
    .out(Cout), .sel({A, B, Cin}));  // open: en
endmodule

module mux_2x1 (
  input  A,
  input  B,
  input  S,
  output out_4
);

  wire and_1_out, and_2_out, not_1_out;

  not not_1 (not_1_out, S);
  and and_1 (and_1_out, A, not_1_out);
  and and_2 (and_2_out, B, S);
  or or_1 (out_4, and_1_out, and_2_out);
endmodule

module mux_8x1 (
  input  A,
  input  B,
  input  S,
  input  in_4,
  input  in_5,
  input  in_6,
  input  in_7,
  input  in_8,
  input  in_9,
  input  in_10,
  input  in_11,
  output out_12
);

  wire and_1_out, and_2_out, and_3_out, and_4_out, and_5_out, and_6_out, and_7_out, and_8_out, not_1_out,
       not_2_out, not_3_out;

  not not_1 (not_1_out, B);
  not not_2 (not_2_out, A);
  not not_3 (not_3_out, S);
  and and_1 (and_1_out, in_4, not_2_out, not_1_out, not_3_out);
  and and_2 (and_2_out, in_5, not_2_out, not_1_out, S);
  and and_3 (and_3_out, in_6, not_2_out, B, not_3_out);
  and and_4 (and_4_out, in_7, not_2_out, B, S);
  and and_5 (and_5_out, in_8, A, not_1_out, not_3_out);
  and and_6 (and_6_out, in_9, A, not_1_out, S);
  and and_7 (and_7_out, in_10, A, B, not_3_out);
  and and_8 (and_8_out, in_11, A, B, S);
  or or_1 (out_12, and_1_out, and_2_out, and_3_out, and_4_out, and_5_out, and_6_out, and_7_out, and_8_out);
endmodule

module somador_mux_8x1 (
  input  A,
  input  B,
  input  Cin,
  output Sum,
  output Cout
);

  mux_8x1 mux_8x1_1 (
    .in_4(1'b0), .in_5(1'b1), .in_6(1'b1), .in_7(1'b0), .in_8(1'b1), .in_9(1'b0), .in_10(1'b0), .in_11(1'b1),
    .A(A), .B(B), .S(Cin), .out_12(Sum));
  mux_8x1 mux_8x1_2 (
    .in_4(1'b0), .in_5(1'b0), .in_6(1'b0), .in_7(1'b1), .in_8(1'b0), .in_9(1'b1), .in_10(1'b1), .in_11(1'b1),
    .A(A), .B(B), .S(Cin), .out_12(Cout));
endmodule

module mux_4x1 (
  input  A,
  input  S,
  input  in_3,
  input  in_4,
  input  in_5,
  input  in_6,
  output out_7
);

  wire and_1_out, and_2_out, and_3_out, and_4_out, not_1_out, not_2_out;

  not not_1 (not_1_out, A);
  not not_2 (not_2_out, S);
  and and_1 (and_1_out, in_3, not_1_out, not_2_out);
  and and_2 (and_2_out, in_4, not_1_out, S);
  and and_3 (and_3_out, in_5, A, not_2_out);
  and and_4 (and_4_out, in_6, A, S);
  or or_1 (out_7, and_1_out, and_2_out, and_3_out, and_4_out);
endmodule

module somador_mux_4x1 (
  input  A,
  input  B,
  input  Cin,
  output Sum,
  output Cout
);

  wire not_1_out;

  not not_1 (not_1_out, Cin);
  mux_4x1 mux_4x1_1 (.in_3(Cin), .in_4(not_1_out), .in_5(not_1_out), .in_6(Cin), .A(A), .S(B), .out_7(Sum));
  mux_4x1 mux_4x1_2 (.in_3(1'b0), .in_4(Cin), .in_5(Cin), .in_6(1'b1), .A(A), .S(B), .out_7(Cout));
endmodule

module somador_8bits_mux_4x1 (
  input  [7:0] in_1,
  input  [7:0] in_2,
  output [7:0] out_3,
  output out_4
);

  wire somador_mux_4x1_1_cout, somador_mux_4x1_2_cout, somador_mux_4x1_3_cout, somador_mux_4x1_4_cout,
       somador_mux_4x1_5_cout, somador_mux_4x1_6_cout, somador_mux_4x1_7_cout;

  somador_mux_4x1 somador_mux_4x1_1 (
    .Sum(out_3[0]), .Cout(somador_mux_4x1_1_cout), .A(in_1[0]), .B(in_2[0]), .Cin(1'b0));
  somador_mux_4x1 somador_mux_4x1_2 (
    .Sum(out_3[1]), .Cout(somador_mux_4x1_2_cout), .A(in_1[1]), .B(in_2[1]), .Cin(somador_mux_4x1_1_cout));
  somador_mux_4x1 somador_mux_4x1_3 (
    .Sum(out_3[2]), .Cout(somador_mux_4x1_3_cout), .A(in_1[2]), .B(in_2[2]), .Cin(somador_mux_4x1_2_cout));
  somador_mux_4x1 somador_mux_4x1_4 (
    .Sum(out_3[3]), .Cout(somador_mux_4x1_4_cout), .A(in_1[3]), .B(in_2[3]), .Cin(somador_mux_4x1_3_cout));
  somador_mux_4x1 somador_mux_4x1_5 (
    .Sum(out_3[4]), .Cout(somador_mux_4x1_5_cout), .A(in_1[4]), .B(in_2[4]), .Cin(somador_mux_4x1_4_cout));
  somador_mux_4x1 somador_mux_4x1_6 (
    .Sum(out_3[5]), .Cout(somador_mux_4x1_6_cout), .A(in_1[5]), .B(in_2[5]), .Cin(somador_mux_4x1_5_cout));
  somador_mux_4x1 somador_mux_4x1_7 (
    .Sum(out_3[6]), .Cout(somador_mux_4x1_7_cout), .A(in_1[6]), .B(in_2[6]), .Cin(somador_mux_4x1_6_cout));
  somador_mux_4x1 somador_mux_4x1_8 (
    .Sum(out_3[7]), .Cout(out_4), .A(in_1[7]), .B(in_2[7]), .Cin(somador_mux_4x1_7_cout));
endmodule
