// Logisim project Relogio digital.circ as structural Verilog: 4 circuits, main circuit main
module main (
  input  [3:0] _0,
  input  [3:0] _10,
  input  [3:0] _6,
  input  [3:0] _4,
  input  [3:0] _3
);

  wire cont_7seg_1_p1, cont_7seg_1_p4, cont_7seg_1_p6, cont_7seg_1_p7, cont_7seg_1_p8, cont_7seg_1_p9,
       cont_7seg_1_p10, cont_7seg_1_p11, cont_7seg_1_p12, cont_7seg_2_p1, cont_7seg_2_p4, cont_7seg_2_p6,
       cont_7seg_2_p8, cont_7seg_2_p9, cont_7seg_2_p11, cont_7seg_2_p12, cont_7seg_2_p13, cont_7seg_3_p1,
       cont_7seg_3_p4, cont_7seg_3_p6, cont_7seg_3_p8, cont_7seg_3_p9, cont_7seg_3_p11, cont_7seg_3_p12,
       cont_7seg_3_p13, cont_7seg_4_p1, cont_7seg_4_p4, cont_7seg_4_p6, cont_7seg_4_p8, cont_7seg_4_p9,
       cont_7seg_4_p11, cont_7seg_4_p12, cont_7seg_4_p13, cont_7seg_5_p1, cont_7seg_5_p4, cont_7seg_5_p6,
       cont_7seg_5_p8, cont_7seg_5_p9, cont_7seg_5_p11, cont_7seg_5_p12, cont_7seg_5_p13, cont_7seg_6_p1,
       cont_7seg_6_p4, cont_7seg_6_p6, cont_7seg_6_p8, cont_7seg_6_p9, cont_7seg_6_p11, cont_7seg_6_p12,
       cont_7seg_6_p13, not_2_out, not_3_out;
  wire [3:0] and_1_out, and_2_out, or_1_out;
  wire [3:3] DH2_out, not_1_out;

  not not_1 (not_1_out[3], DH2_out[3]);
  assign and_1_out = _10 & {4{not_1_out[3]}};  // AND_Gate and_1, 4 bits wide
  assign and_2_out = _4 & {4{DH2_out[3]}};  // AND_Gate and_2, 4 bits wide
  not not_2 (not_2_out, cont_7seg_1_p10);
  and DH2 (DH2_out[3], cont_7seg_1_p12, cont_7seg_1_p11, not_2_out, cont_7seg_1_p9, cont_7seg_1_p8, not_3_out, cont_7seg_1_p4);
  not not_3 (not_3_out, cont_7seg_1_p6);
  assign or_1_out = and_1_out | and_2_out;  // OR_Gate or_1, 4 bits wide
  // cont_7seg cont_7seg_1: pin names not known; wires that end beside it: cont_7seg_1_p1, _0, _3, cont_7seg_1_p4, 1'b1, cont_7seg_1_p6, cont_7seg_1_p7, cont_7seg_1_p8, cont_7seg_1_p9, cont_7seg_1_p10, cont_7seg_1_p11, cont_7seg_1_p12
  _7_Segment_Display u_7_segment_display_1 (
    .g(cont_7seg_1_p4), .f(cont_7seg_1_p6), .a(cont_7seg_1_p12), .b(cont_7seg_1_p11), .e(cont_7seg_1_p8),
    .d(cont_7seg_1_p9), .c(cont_7seg_1_p10));  // open: dp
  // cont_7seg cont_7seg_2: pin names not known; wires that end beside it: cont_7seg_2_p1, _0, or_1_out, cont_7seg_2_p4, 1'b1, cont_7seg_2_p6, cont_7seg_1_p7, cont_7seg_2_p8, cont_7seg_2_p9, cont_7seg_1_p1, cont_7seg_2_p11, cont_7seg_2_p12, cont_7seg_2_p13
  _7_Segment_Display u_7_segment_display_2 (
    .g(cont_7seg_2_p4), .f(cont_7seg_2_p6), .a(cont_7seg_2_p13), .b(cont_7seg_2_p12), .e(cont_7seg_2_p8),
    .d(cont_7seg_2_p9), .c(cont_7seg_2_p11));  // open: dp
  _7_Segment_Display u_7_segment_display_3 (
    .g(cont_7seg_3_p4), .f(cont_7seg_3_p6), .a(cont_7seg_3_p13), .b(cont_7seg_3_p12), .e(cont_7seg_3_p8),
    .d(cont_7seg_3_p9), .c(cont_7seg_3_p11));  // open: dp
  // cont_7seg cont_7seg_3: pin names not known; wires that end beside it: cont_7seg_3_p1, _0, _6, cont_7seg_3_p4, 1'b1, cont_7seg_3_p6, cont_7seg_1_p7, cont_7seg_3_p8, cont_7seg_3_p9, cont_7seg_2_p1, cont_7seg_3_p11, cont_7seg_3_p12, cont_7seg_3_p13
  _7_Segment_Display u_7_segment_display_4 (
    .g(cont_7seg_4_p4), .f(cont_7seg_4_p6), .a(cont_7seg_4_p13), .b(cont_7seg_4_p12), .e(cont_7seg_4_p8),
    .d(cont_7seg_4_p9), .c(cont_7seg_4_p11));  // open: dp
  // cont_7seg cont_7seg_4: pin names not known; wires that end beside it: cont_7seg_4_p1, _0, _10, cont_7seg_4_p4, 1'b1, cont_7seg_4_p6, cont_7seg_1_p7, cont_7seg_4_p8, cont_7seg_4_p9, cont_7seg_3_p1, cont_7seg_4_p11, cont_7seg_4_p12, cont_7seg_4_p13
  // cont_7seg cont_7seg_5: pin names not known; wires that end beside it: cont_7seg_5_p1, _0, _6, cont_7seg_5_p4, 1'b1, cont_7seg_5_p6, cont_7seg_1_p7, cont_7seg_5_p8, cont_7seg_5_p9, cont_7seg_4_p1, cont_7seg_5_p11, cont_7seg_5_p12, cont_7seg_5_p13
  _7_Segment_Display u_7_segment_display_5 (
    .g(cont_7seg_5_p4), .f(cont_7seg_5_p6), .a(cont_7seg_5_p13), .b(cont_7seg_5_p12), .e(cont_7seg_5_p8),
    .d(cont_7seg_5_p9), .c(cont_7seg_5_p11));  // open: dp
  _7_Segment_Display u_7_segment_display_6 (
    .g(cont_7seg_6_p4), .f(cont_7seg_6_p6), .a(cont_7seg_6_p13), .b(cont_7seg_6_p12), .e(cont_7seg_6_p8),
    .d(cont_7seg_6_p9), .c(cont_7seg_6_p11));  // open: dp
  // cont_7seg cont_7seg_6: pin names not known; wires that end beside it: cont_7seg_6_p1, _0, _10, cont_7seg_6_p4, 1'b1, cont_7seg_6_p6, cont_7seg_1_p7, cont_7seg_6_p8, cont_7seg_6_p9, cont_7seg_5_p1, cont_7seg_6_p11, cont_7seg_6_p12, cont_7seg_6_p13
  Button RESET (.out(cont_7seg_1_p7));
  Clock clock_1 (.out(cont_7seg_6_p1));

  // Notes on the sheet:
  //   RELÓGIO DIGITAL
endmodule

module _7segment (
);

  wire multiplexer_1_out, multiplexer_2_out, multiplexer_3_out, multiplexer_4_out, multiplexer_5_out,
       multiplexer_6_out, multiplexer_7_out;
  wire [3:0] undriven;

  Multiplexer #(.select(4)) multiplexer_1 (
    .in0(1'b1), .in1(1'b0), .in2(1'b1), .in3(1'b1), .in4(1'b0), .in5(1'b1), .in6(1'b1), .in7(1'b1),
    .in8(1'b1), .in9(1'b1), .in10(1'b1), .in11(1'b0), .in12(1'b1), .in13(1'b0), .in14(1'b1), .in15(1'b1),
    .out(multiplexer_1_out), .sel(undriven));  // open: en
  Multiplexer #(.select(4)) multiplexer_2 (
    .in0(1'b1), .in1(1'b1), .in2(1'b1), .in3(1'b1), .in4(1'b1), .in5(1'b0), .in6(1'b0), .in7(1'b1),
    .in8(1'b1), .in9(1'b1), .in10(1'b1), .in11(1'b0), .in12(1'b0), .in13(1'b1), .in14(1'b0), .in15(1'b0),
    .out(multiplexer_2_out), .sel(undriven));  // open: en
  Multiplexer #(.select(4)) multiplexer_3 (
    .in0(1'b1), .in1(1'b1), .in2(1'b0), .in3(1'b1), .in4(1'b1), .in5(1'b1), .in6(1'b1), .in7(1'b1),
    .in8(1'b1), .in9(1'b1), .in10(1'b1), .in11(1'b1), .in12(1'b0), .in13(1'b1), .in14(1'b0), .in15(1'b0),
    .out(multiplexer_3_out), .sel(undriven));  // open: en
  Multiplexer #(.select(4)) multiplexer_4 (
    .in0(1'b1), .in1(1'b0), .in2(1'b1), .in3(1'b1), .in4(1'b0), .in5(1'b1), .in6(1'b1), .in7(1'b0),
    .in8(1'b1), .in9(1'b1), .in10(1'b0), .in11(1'b1), .in12(1'b1), .in13(1'b1), .in14(1'b1), .in15(1'b0),
    .out(multiplexer_4_out), .sel(undriven));  // open: en
  Multiplexer #(.select(4)) multiplexer_5 (
    .in0(1'b1), .in1(1'b0), .in2(1'b1), .in3(1'b0), .in4(1'b0), .in5(1'b0), .in6(1'b1), .in7(1'b0),
    .in8(1'b1), .in9(1'b0), .in10(1'b1), .in11(1'b1), .in12(1'b1), .in13(1'b1), .in14(1'b1), .in15(1'b1),
    .out(multiplexer_5_out), .sel(undriven));  // open: en
  Multiplexer #(.select(4)) multiplexer_6 (
    .in0(1'b1), .in1(1'b0), .in2(1'b0), .in3(1'b0), .in4(1'b1), .in5(1'b1), .in6(1'b1), .in7(1'b0),
    .in8(1'b1), .in9(1'b1), .in10(1'b1), .in11(1'b1), .in12(1'b1), .in13(1'b0), .in14(1'b1), .in15(1'b1),
    .out(multiplexer_6_out), .sel(undriven));  // open: en
  Multiplexer #(.select(4)) multiplexer_7 (
    .in0(1'b0), .in1(1'b0), .in2(1'b1), .in3(1'b1), .in4(1'b1), .in5(1'b1), .in6(1'b1), .in7(1'b0),
    .in8(1'b1), .in9(1'b1), .in10(1'b1), .in11(1'b1), .in12(1'b0), .in13(1'b1), .in14(1'b1), .in15(1'b1),
    .out(multiplexer_7_out), .sel(undriven));  // open: en
  _7_Segment_Display u_7_segment_display_1 (
    .g(multiplexer_7_out), .f(multiplexer_6_out), .a(multiplexer_1_out), .b(multiplexer_2_out),
    .e(multiplexer_5_out), .d(multiplexer_4_out), .c(multiplexer_3_out));  // open: dp

  // Notes on the sheet:
  //   MUX 7 SEGMENTOS
endmodule

module contMN (
  input  Power,
  input  Clk,
  input  [3:0] init,
  input  [3:0] \end ,
  input  RstExt,
  output S3,
  output S2,
  output S1,
  output S0,
  output Reset
);

  wire demultiplexer_1_out0, demultiplexer_1_out1, demultiplexer_2_out0, demultiplexer_2_out1,
       demultiplexer_3_out0, demultiplexer_3_out1, demultiplexer_4_out0, demultiplexer_4_out1, or_1_out,
       xnor_1_out, xnor_2_out, xnor_3_out, xnor_4_out;

  J_K_Flip_Flop j_k_ff_1 (
    .J(Power), .clk(Clk), .K(Power), .Q(S0), .preset(demultiplexer_1_out1), .reset(demultiplexer_1_out0));  // open: Qn, en
  Demultiplexer demultiplexer_1 (
    .out0(demultiplexer_1_out0), .out1(demultiplexer_1_out1), .in(or_1_out), .sel(init[0]));  // open: en
  or or_1 (or_1_out, RstExt, Reset);
  T_Flip_Flop #(.trigger("falling")) t_ff_1 (
    .clk(S0), .T(1'b1), .Q(S1), .preset(demultiplexer_2_out1), .reset(demultiplexer_2_out0));  // open: Qn, en
  Demultiplexer demultiplexer_2 (
    .out0(demultiplexer_2_out0), .out1(demultiplexer_2_out1), .in(or_1_out), .sel(init[1]));  // open: en
  xnor xnor_1 (xnor_1_out, \end [0], S0);
  xnor xnor_2 (xnor_2_out, \end [1], S1);
  and and_1 (Reset, xnor_1_out, xnor_2_out, xnor_3_out, xnor_4_out);
  Demultiplexer demultiplexer_3 (
    .out0(demultiplexer_3_out0), .out1(demultiplexer_3_out1), .in(or_1_out), .sel(init[2]));  // open: en
  xnor xnor_3 (xnor_3_out, \end [2], S2);
  T_Flip_Flop #(.trigger("falling")) t_ff_2 (
    .clk(S1), .T(1'b1), .Q(S2), .preset(demultiplexer_3_out1), .reset(demultiplexer_3_out0));  // open: Qn, en
  T_Flip_Flop #(.trigger("falling")) t_ff_3 (
    .clk(S2), .T(1'b1), .Q(S3), .preset(demultiplexer_4_out1), .reset(demultiplexer_4_out0));  // open: Qn, en
  Demultiplexer demultiplexer_4 (
    .out0(demultiplexer_4_out0), .out1(demultiplexer_4_out1), .in(or_1_out), .sel(init[3]));  // open: en
  xnor xnor_4 (xnor_4_out, \end [3], S3);

  // Notes on the sheet:
  //   CONTADOR MN
endmodule

module cont_7seg (
  input  Power,
  input  Clk,
  input  [3:0] Init,
  input  [3:0] End,
  input  RstExt,
  output G,
  output F,
  output E,
  output D,
  output C,
  output B,
  output A,
  output Reset
);

  wire [3:0] contmn_1_s0;

  Multiplexer #(.select(4)) multiplexer_1 (
    .in0(1'b1), .in1(1'b0), .in2(1'b1), .in3(1'b1), .in4(1'b0), .in5(1'b1), .in6(1'b1), .in7(1'b1),
    .in8(1'b1), .in9(1'b1), .in10(1'b1), .in11(1'b0), .in12(1'b1), .in13(1'b0), .in14(1'b1), .in15(1'b1),
    .out(A), .sel(contmn_1_s0));  // open: en
  Multiplexer #(.select(4)) multiplexer_2 (
    .in0(1'b1), .in1(1'b1), .in2(1'b1), .in3(1'b1), .in4(1'b1), .in5(1'b0), .in6(1'b0), .in7(1'b1),
    .in8(1'b1), .in9(1'b1), .in10(1'b1), .in11(1'b0), .in12(1'b0), .in13(1'b1), .in14(1'b0), .in15(1'b0),
    .out(B), .sel(contmn_1_s0));  // open: en
  Multiplexer #(.select(4)) multiplexer_3 (
    .in0(1'b1), .in1(1'b1), .in2(1'b0), .in3(1'b1), .in4(1'b1), .in5(1'b1), .in6(1'b1), .in7(1'b1),
    .in8(1'b1), .in9(1'b1), .in10(1'b1), .in11(1'b1), .in12(1'b0), .in13(1'b1), .in14(1'b0), .in15(1'b0),
    .out(C), .sel(contmn_1_s0));  // open: en
  contMN contmn_1 (
    .init(Init), .\end (End), .S3(contmn_1_s0[3]), .S2(contmn_1_s0[2]), .S1(contmn_1_s0[1]),
    .S0(contmn_1_s0[0]), .Clk(Clk), .Power(Power), .Reset(Reset), .RstExt(RstExt));
  Multiplexer #(.select(4)) multiplexer_4 (
    .in0(1'b1), .in1(1'b0), .in2(1'b1), .in3(1'b1), .in4(1'b0), .in5(1'b1), .in6(1'b1), .in7(1'b0),
    .in8(1'b1), .in9(1'b1), .in10(1'b0), .in11(1'b1), .in12(1'b1), .in13(1'b1), .in14(1'b1), .in15(1'b0),
    .out(D), .sel(contmn_1_s0));  // open: en
  Multiplexer #(.select(4)) multiplexer_5 (
    .in0(1'b1), .in1(1'b0), .in2(1'b1), .in3(1'b0), .in4(1'b0), .in5(1'b0), .in6(1'b1), .in7(1'b0),
    .in8(1'b1), .in9(1'b0), .in10(1'b1), .in11(1'b1), .in12(1'b1), .in13(1'b1), .in14(1'b1), .in15(1'b1),
    .out(E), .sel(contmn_1_s0));  // open: en
  Multiplexer #(.select(4)) multiplexer_6 (
    .in0(1'b1), .in1(1'b0), .in2(1'b0), .in3(1'b0), .in4(1'b1), .in5(1'b1), .in6(1'b1), .in7(1'b0),
    .in8(1'b1), .in9(1'b1), .in10(1'b1), .in11(1'b1), .in12(1'b1), .in13(1'b0), .in14(1'b1), .in15(1'b1),
    .out(F), .sel(contmn_1_s0));  // open: en
  Multiplexer #(.select(4)) multiplexer_7 (
    .in0(1'b0), .in1(1'b0), .in2(1'b1), .in3(1'b1), .in4(1'b1), .in5(1'b1), .in6(1'b1), .in7(1'b0),
    .in8(1'b1), .in9(1'b1), .in10(1'b1), .in11(1'b1), .in12(1'b0), .in13(1'b1), .in14(1'b1), .in15(1'b1),
    .out(G), .sel(contmn_1_s0));  // open: en

  // Notes on the sheet:
  //   MUX 7 SEGMENTOS + CONTADOR MN
endmodule
