// Logisim project contadoresHardcore.circ as structural Verilog: 5 circuits, main circuit main
module main (
);

  J_K_Flip_Flop j_k_ff_1 ();  // open: J, clk, K, Q, Qn, preset, en, reset
endmodule

module cont10 (
  output out_1,
  output out_2,
  output out_3,
  output out_4
);

  wire and_1_out, clock_1_out;

  Clock clock_1 (.out(clock_1_out));
  T_Flip_Flop #(.trigger("falling")) t_ff_1 (
    .clk(clock_1_out), .T(1'b1), .Q(out_4), .reset(and_1_out));  // open: Qn, preset, en
  T_Flip_Flop #(.trigger("falling")) t_ff_2 (
    .clk(out_4), .T(1'b1), .Q(out_3), .reset(and_1_out));  // open: Qn, preset, en
  T_Flip_Flop #(.trigger("falling")) t_ff_3 (
    .clk(out_3), .T(1'b1), .Q(out_2), .reset(and_1_out));  // open: Qn, preset, en
  and and_1 (and_1_out, out_1, ~out_2, out_3, ~out_4);  // AND_Gate
  T_Flip_Flop #(.trigger("falling")) t_ff_4 (
    .clk(out_2), .T(1'b1), .Q(out_1), .reset(and_1_out));  // open: Qn, preset, en
endmodule

module combin (
  output out_1,
  output out_2,
  output out_3,
  output out_4
);

  wire clock_1_out;

  Clock clock_1 (.out(clock_1_out));
  T_Flip_Flop #(.trigger("falling")) t_ff_1 (.clk(clock_1_out), .T(1'b1), .Q(out_4));  // open: Qn, preset, reset, en
  T_Flip_Flop #(.trigger("falling")) t_ff_2 (.clk(out_4), .T(1'b1), .Q(out_3));  // open: Qn, preset, reset, en
  T_Flip_Flop #(.trigger("falling")) t_ff_3 (.clk(out_3), .T(1'b1), .Q(out_2));  // open: Qn, preset, reset, en
  T_Flip_Flop #(.trigger("falling")) t_ff_4 (.clk(out_2), .T(1'b1), .Q(out_1));  // open: Qn, preset, reset, en
endmodule

module cont3_11 (
  output out_1,
  output out_2,
  output out_3,
  output out_4
);

  wire and_1_out, clock_1_out;

  Clock clock_1 (.out(clock_1_out));
  J_K_Flip_Flop j_k_ff_1 (.J(1'b1), .clk(clock_1_out), .K(1'b1), .Q(out_4), .preset(and_1_out));  // open: Qn, en, reset
  T_Flip_Flop #(.trigger("falling")) t_ff_1 (
    .clk(out_4), .T(1'b1), .Q(out_3), .preset(and_1_out));  // open: Qn, reset, en
  and and_1 (and_1_out, out_1, out_2, ~out_3, ~out_4);  // AND_Gate
  T_Flip_Flop #(.trigger("falling")) t_ff_2 (
    .clk(out_3), .T(1'b1), .Q(out_2), .reset(and_1_out));  // open: Qn, preset, en
  T_Flip_Flop #(.trigger("falling")) t_ff_3 (
    .clk(out_2), .T(1'b1), .Q(out_1), .reset(and_1_out));  // open: Qn, preset, en
endmodule

module contMN (
  input  [3:0] init,
  input  [3:0] \end ,
  output out_3,
  output out_4,
  output out_5,
  output out_6
);

  wire and_1_out, clock_1_out, demultiplexer_1_out0, demultiplexer_1_out1, demultiplexer_2_out0,
       demultiplexer_2_out1, demultiplexer_3_out0, demultiplexer_3_out1, demultiplexer_4_out0,
       demultiplexer_4_out1, xnor_1_out, xnor_2_out, xnor_3_out, xnor_4_out;

  Clock clock_1 (.out(clock_1_out));
  Demultiplexer demultiplexer_1 (
    .out0(demultiplexer_1_out0), .out1(demultiplexer_1_out1), .in(and_1_out), .sel(init[0]));  // open: en
  J_K_Flip_Flop j_k_ff_1 (
    .J(1'b1), .clk(clock_1_out), .K(1'b1), .Q(out_6), .preset(demultiplexer_1_out1),
    .reset(demultiplexer_1_out0));  // open: Qn, en
  xnor xnor_1 (xnor_1_out, \end [0], out_6);
  and and_1 (and_1_out, xnor_1_out, xnor_2_out, xnor_3_out, xnor_4_out);
  T_Flip_Flop #(.trigger("falling")) t_ff_1 (
    .clk(out_6), .T(1'b1), .Q(out_5), .preset(demultiplexer_2_out1), .reset(demultiplexer_2_out0));  // open: Qn, en
  Demultiplexer demultiplexer_2 (
    .out0(demultiplexer_2_out0), .out1(demultiplexer_2_out1), .in(and_1_out), .sel(init[1]));  // open: en
  xnor xnor_2 (xnor_2_out, \end [1], out_5);
  T_Flip_Flop #(.trigger("falling")) t_ff_2 (
    .clk(out_5), .T(1'b1), .Q(out_4), .preset(demultiplexer_3_out1), .reset(demultiplexer_3_out0));  // open: Qn, en
  Demultiplexer demultiplexer_3 (
    .out0(demultiplexer_3_out0), .out1(demultiplexer_3_out1), .in(and_1_out), .sel(init[2]));  // open: en
  xnor xnor_3 (xnor_3_out, \end [2], out_4);
  T_Flip_Flop #(.trigger("falling")) t_ff_3 (
    .clk(out_4), .T(1'b1), .Q(out_3), .preset(demultiplexer_4_out1), .reset(demultiplexer_4_out0));  // open: Qn, en
  Demultiplexer demultiplexer_4 (
    .out0(demultiplexer_4_out0), .out1(demultiplexer_4_out1), .in(and_1_out), .sel(init[3]));  // open: en
  xnor xnor_4 (xnor_4_out, \end [3], out_3);
endmodule
