// Logisim project memorias.circ as structural Verilog: 6 circuits, main circuit main
module main (
  input  in_1,
  input  in_2,
  input  [7:0] E,
  input  in_4,
  input  [7:0] E_2,
  input  [1:0] in_6,
  input  in_7,
  output out_8,
  output out_9,
  output [7:0] Q,
  output [7:0] Q_2
);

  wire clock_1_out, clock_2_out, clock_3_out;

  Clock clock_1 (.out(clock_1_out));
  Clock clock_2 (.out(clock_2_out));
  Clock clock_3 (.out(clock_3_out));
  D_Flip_Flop #(.trigger("falling")) d_ff_1 (
    .clk(clock_1_out), .D(in_1), .Q(out_8), .Qn(out_9));  // open: preset, en, reset
  registrador8b registrador8b_1 (.clk(clock_2_out), .E(E), .Q(Q), .en(in_4), .clear(in_2));
  memoria memoria_1 (.clk(clock_3_out), .Din(E_2), .addr(in_6), .write(in_7), .Dout(Q_2), .clear(in_7));
endmodule

module registrador8b (
  input  clk,
  input  clear,
  input  [7:0] E,
  input  en,
  output [7:0] Q
);

  D_Flip_Flop d_ff_1 (.clk(clk), .D(E[0]), .Q(Q[0]), .en(en), .reset(clear));  // open: Qn, preset
  D_Flip_Flop d_ff_2 (.clk(clk), .D(E[1]), .Q(Q[1]), .en(en), .reset(clear));  // open: Qn, preset
  D_Flip_Flop d_ff_3 (.clk(clk), .D(E[2]), .Q(Q[2]), .en(en), .reset(clear));  // open: Qn, preset
  D_Flip_Flop d_ff_4 (.clk(clk), .D(E[3]), .Q(Q[3]), .en(en), .reset(clear));  // open: Qn, preset
  D_Flip_Flop d_ff_5 (.clk(clk), .D(E[4]), .Q(Q[4]), .en(en), .reset(clear));  // open: Qn, preset
  D_Flip_Flop d_ff_6 (.clk(clk), .D(E[5]), .Q(Q[5]), .en(en), .reset(clear));  // open: Qn, preset
  D_Flip_Flop d_ff_7 (.clk(clk), .D(E[6]), .Q(Q[6]), .en(en), .reset(clear));  // open: Qn, preset
  D_Flip_Flop d_ff_8 (.clk(clk), .D(E[7]), .Q(Q[7]), .en(en), .reset(clear));  // open: Qn, preset
endmodule

module memoria (
  input  clk,
  input  [7:0] Din,
  input  [1:0] addr,
  input  write,
  input  clear,
  output [7:0] Dout
);

  wire and_1_out, and_2_out, and_3_out, and_4_out, and_5_out, and_6_out, and_7_out, and_8_out;
  wire [7:0] register_1_q, register_2_q, register_3_q, register_4_q;

  and and_1 (and_1_out, ~addr[0], ~addr[1]);  // AND_Gate
  and and_2 (and_2_out, addr[0], ~addr[1]);  // AND_Gate
  and and_3 (and_3_out, ~addr[0], addr[1]);  // AND_Gate
  and and_4 (and_4_out, addr[0], addr[1]);
  and and_5 (and_5_out, and_1_out, write);
  and and_6 (and_6_out, and_2_out, write);
  and and_7 (and_7_out, and_3_out, write);
  and and_8 (and_8_out, and_4_out, write);
  Register register_1 (.D(Din), .en(and_5_out), .Q(register_1_q), .clk(clk), .clr(clear));
  Register register_2 (.D(Din), .en(and_6_out), .Q(register_2_q), .clk(clk), .clr(clear));
  Register register_3 (.D(Din), .en(and_7_out), .Q(register_3_q), .clk(clk), .clr(clear));
  Register register_4 (.D(Din), .en(and_8_out), .Q(register_4_q), .clk(clk), .clr(clear));
  Multiplexer #(.select(2), .width(8)) multiplexer_1 (
    .in0(register_1_q), .in1(register_2_q), .in2(register_3_q), .in3(register_4_q), .out(Dout), .sel(addr));  // open: en
endmodule

module ROM (
  input  [1:0] addr,
  output [7:0] Dout
);

  Multiplexer #(.select(2), .width(8)) multiplexer_1 (
    .in0(8'haa), .in1(8'hf0), .in2(8'h30), .in3(8'h77), .out(Dout), .sel(addr));  // open: en

  // Notes on the sheet:
  //   10101010
  //   11110000
  //   00110000
  //   01110111
endmodule

module regdesl (
  input  b7,
  input  in_2
);

  wire d_ff_2_q, d_ff_3_q, d_ff_4_q, d_ff_5_q, d_ff_6_q, d_ff_7_q, d_ff_8_q;

  D_Flip_Flop d_ff_1 (.clk(b7), .D(d_ff_2_q));  // open: Q, Qn, preset, en, reset
  D_Flip_Flop d_ff_2 (.clk(b7), .D(d_ff_3_q), .Q(d_ff_2_q));  // open: Qn, preset, en, reset
  D_Flip_Flop d_ff_3 (.clk(b7), .D(d_ff_4_q), .Q(d_ff_3_q));  // open: Qn, preset, en, reset
  D_Flip_Flop d_ff_4 (.clk(b7), .D(d_ff_5_q), .Q(d_ff_4_q));  // open: Qn, preset, en, reset
  D_Flip_Flop d_ff_5 (.clk(b7), .D(d_ff_6_q), .Q(d_ff_5_q));  // open: Qn, preset, en, reset
  D_Flip_Flop d_ff_6 (.clk(b7), .D(d_ff_7_q), .Q(d_ff_6_q));  // open: Qn, preset, en, reset
  D_Flip_Flop d_ff_7 (.clk(b7), .D(d_ff_8_q), .Q(d_ff_7_q));  // open: Qn, preset, en, reset
  D_Flip_Flop d_ff_8 (.clk(b7), .D(in_2), .Q(d_ff_8_q));  // open: Qn, preset, en, reset

  // Notes on the sheet:
  //   b0
endmodule

module regdesldiresq (
  input  clk,
  input  dir
);

  wire d_ff_1_q, d_ff_2_q, d_ff_3_q, multiplexer_1_out, multiplexer_2_out, multiplexer_3_out;

  Multiplexer multiplexer_1 (.in0(d_ff_2_q), .in1(1'b0), .out(multiplexer_1_out), .sel(dir));  // open: en
  D_Flip_Flop d_ff_1 (.clk(clk), .D(multiplexer_1_out), .Q(d_ff_1_q));  // open: Qn, preset, en, reset
  D_Flip_Flop d_ff_2 (.clk(clk), .D(multiplexer_2_out), .Q(d_ff_2_q));  // open: Qn, preset, en, reset
  Multiplexer multiplexer_2 (.in0(d_ff_3_q), .in1(d_ff_1_q), .out(multiplexer_2_out), .sel(dir));  // open: en
  Multiplexer multiplexer_3 (.in0(1'b0), .in1(d_ff_2_q), .out(multiplexer_3_out), .sel(dir));  // open: en
  D_Flip_Flop d_ff_3 (.clk(clk), .D(multiplexer_3_out), .Q(d_ff_3_q));  // open: Qn, preset, en, reset

  // Notes on the sheet:
  //   esq=0 / dir =1
  //   b2
  //   b1
  //   b0
endmodule
